# Fritzing sketch phtemp (saved by Fritzing 0.9.2b)
breadboards: 1

parts:
  Part1 = Arduino Nano (Rev3.0)
  pH_Circuit1 = pH Circuit
  Pre-Assembled_Female_BNC1 = Pre-Assembled Female BNC
  Conductivity_Circuit1 = Conductivity Circuit
  Pre-Assembled_Female_BNC2 = Pre-Assembled Female BNC
  NRF24L1 = NRF24L01
  R1 = Resistor [tolerance=±5% resistance=4.7k package=THT]
  DS1 = DS18B20 1-Wire Temperature Sensor Probe Cable
  DHT1 = DHT22 Humidity and Temperature Sensor
  DividerLow = Antenna
  dividerHigh = Antenna
  R2 = Resistor [tolerance=±5% resistance=4.7k package=THT]

nets:
  GND: Part1.GND, pH_Circuit1.GND#0, Conductivity_Circuit1.GND#0, NRF24L1.GND, DS1.GND, DHT1.GND
  N1: Part1.D2, DHT1.DATA
  N2: Part1.D3, R1.Pin_1, DS1.DQ
  N3: Part1.D7, R2.Pin_1
  N4: Part1.D8, dividerHigh.antenna_lead
  N5: Part1.D9, NRF24L1.CE
  N6: Part1.D10, NRF24L1.CSN
  N7: Part1.D11/MOSI, NRF24L1.MOSI
  N8: Part1.D12/MISO, NRF24L1.MISO
  N9: Part1.A5, pH_Circuit1.RX, Conductivity_Circuit1.RX
  N10: Part1.A4, pH_Circuit1.TX, Conductivity_Circuit1.TX
  N11: Part1.A0, DividerLow.antenna_lead, R2.Pin_0
  VCC: Part1.3V3, pH_Circuit1.Vcc, Conductivity_Circuit1.Vcc, NRF24L1.VCC, R1.Pin_0, DHT1.VDD
  N12: Part1.D13/SCK, NRF24L1.SCK
  N13: pH_Circuit1.PRB, Pre-Assembled_Female_BNC1.PRB
  N14: pH_Circuit1.GND#5, Pre-Assembled_Female_BNC1.GND
  N15: Conductivity_Circuit1.PRB, Pre-Assembled_Female_BNC2.PRB
  N16: Conductivity_Circuit1.GND#5, Pre-Assembled_Female_BNC2.GND

custom parts:
  NRF24L01: NRF24L01 module
