# Fritzing sketch relaynano (saved by Fritzing 0.9.2b)
circuit board: 8.46667cm x 5.64444cm
breadboards: 1

parts:
  Part1 = Arduino Nano (Rev3.0)
  NRF24L1 = NRF24L01
  KY-1 = Keyes Relay [package=THT]
  KY-2 = Keyes Relay [package=THT]
  KY-3 = Keyes Relay [package=THT]
  KY-4 = Keyes Relay [package=THT]
  KY-5 = Keyes Relay [package=THT]
  KY-6 = Keyes Relay [package=THT]
  KY-7 = Keyes Relay [package=THT]
  KY-8 = Keyes Relay [package=THT]

nets:
  GND: Part1.GND, NRF24L1.GND, KY-1.ground, KY-2.ground, KY-3.ground, KY-4.ground, KY-5.ground, KY-6.ground, KY-7.ground, KY-8.ground
  N1: Part1.D9, NRF24L1.CE
  N2: Part1.D10, NRF24L1.CSN
  N3: Part1.D11/MOSI, NRF24L1.MOSI
  N4: Part1.D12/MISO, NRF24L1.MISO
  N5: Part1.5V, KY-1.power, KY-2.power, KY-3.power, KY-4.power, KY-5.power, KY-6.power, KY-7.power, KY-8.power
  N6: Part1.A7, KY-6.signal
  N7: Part1.A6, KY-8.signal
  N8: Part1.A5, KY-7.signal
  N9: Part1.A4, KY-5.signal
  N10: Part1.A3, KY-4.signal
  N11: Part1.A2, KY-3.signal
  N12: Part1.A1, KY-2.signal
  N13: Part1.A0, KY-1.signal
  3V3: Part1.3V3, NRF24L1.VCC
  N14: Part1.D13/SCK, NRF24L1.SCK

custom parts:
  NRF24L01: NRF24L01 module
  Keyes Relay: The Keyes 5V relay module is suitable for SCM development, home appliance control. It uses a 5V~12V TIL control signal which can control DC / AC signal.
